# Fritzing sketch driver-drv2605-i2c-atmega328p (saved by Fritzing 0.9.3b)

parts:
  Arduino_Uno = Arduino Uno (Rev3)
  Part1 = Adafruit DRV2605L [part_number="Adafruit #2305"]
  MOTOR1 = Vibration Motor

nets:
  N1: Arduino_Uno.A4/SDA, Part1.SDA
  N2: Arduino_Uno.A5/SCL, Part1.SCL
  5V: Arduino_Uno.5V, Part1.VIN
  GND: Arduino_Uno.GND, Part1.GND
  N3: Part1.OUT+, MOTOR1.POS
  N4: Part1.OUT-, MOTOR1.NEG

notes:
  C10-100
  4 mm LRA
  Arduino Uno
  DRV2605L
  Breakout Board

custom parts:
  Adafruit DRV2605L: The DRV2605 from TI is a fancy little motor driver. Rather than controlling a stepper motor or DC motor, its designed specifically for controlling haptic motors - buzzers and vibration motors. Normally one would just turn those kinds of motors on and off, but this driver has the ability to have various effects when driving a vibe motor. For example, ramping the vibration level up and down,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
  Vibration Motor: An eccentric vibration motor!
